// Logisim project Digital Logic Project.circ as structural Verilog: 11 circuits, main circuit main
module main (
  input  S1,
  input  S0,
  input  S2,
  input  S3,
  input  A0,
  input  A1,
  input  A2,
  input  A3,
  input  B0,
  input  B1,
  input  B2,
  input  B3,
  output Y0,
  output V,
  output Y1,
  output Y2,
  output Y3,
  output Z
);

  wire n2_1_mux_1_out_4, n2_1_mux_2_out_4, n2_1_mux_3_out_4, n2_1_mux_4_out_4, n4bit_au_1_v, n4bit_au_1_y0,
       n4bit_au_1_y1, n4bit_au_1_y2, n4bit_au_1_y3, n4bit_lu_1_out_11, n4bit_lu_1_out_12, n4bit_lu_1_out_13,
       n4bit_lu_1_out_14, not_1_out, not_2_out, not_3_out, not_4_out, not_5_out, shifter_1_s0, shifter_1_s1,
       shifter_1_s2, shifter_1_s3;

  shifter shifter_1 (
    .A0(A0), .A1(A1), .A2(A2), .A3(A3), .S0(shifter_1_s0), .S1(shifter_1_s1), .S2(shifter_1_s2),
    .S3(shifter_1_s3));
  _4Bit_LU u_4bit_lu_1 (
    .in_3(A0), .in_4(B0), .in_5(A1), .in_6(B1), .in_7(A2), .in_8(B2), .in_9(A3), .in_10(B3),
    .out_11(n4bit_lu_1_out_11), .out_12(n4bit_lu_1_out_12), .out_13(n4bit_lu_1_out_13),
    .out_14(n4bit_lu_1_out_14), .S0(S1), .S1(S0));
  _4Bit_AU u_4bit_au_1 (
    .A0(A0), .B0(B0), .B1(B1), .A2(A2), .B2(B2), .A3(A3), .B3(B3), .Y0(n4bit_au_1_y0), .Y1(n4bit_au_1_y1),
    .Y2(n4bit_au_1_y2), .Y3(n4bit_au_1_y3), .V(n4bit_au_1_v), .S0(S0), .Cin(S1), .A1(A1));
  not not_1 (not_1_out, S3);
  and and_1 (V, n4bit_au_1_v, S2, not_1_out, S0);
  _2_1_Mux u_2_1_mux_1 (.Selector(S2), .A(n4bit_au_1_y3), .B(n4bit_lu_1_out_11), .out_4(n2_1_mux_1_out_4));
  _2_1_Mux u_2_1_mux_2 (.Selector(S2), .A(n4bit_au_1_y2), .B(n4bit_lu_1_out_12), .out_4(n2_1_mux_2_out_4));
  _2_1_Mux u_2_1_mux_3 (.Selector(S2), .A(n4bit_au_1_y1), .B(n4bit_lu_1_out_13), .out_4(n2_1_mux_3_out_4));
  _2_1_Mux u_2_1_mux_4 (.Selector(S2), .A(n4bit_au_1_y0), .B(n4bit_lu_1_out_14), .out_4(n2_1_mux_4_out_4));
  _2_1_Mux u_2_1_mux_5 (.Selector(S3), .A(shifter_1_s0), .B(n2_1_mux_1_out_4), .out_4(Y0));
  _2_1_Mux u_2_1_mux_6 (.Selector(S3), .A(shifter_1_s1), .B(n2_1_mux_2_out_4), .out_4(Y1));
  _2_1_Mux u_2_1_mux_7 (.Selector(S3), .A(shifter_1_s2), .B(n2_1_mux_3_out_4), .out_4(Y2));
  _2_1_Mux u_2_1_mux_8 (.Selector(S3), .A(shifter_1_s3), .B(n2_1_mux_4_out_4), .out_4(Y3));
  not not_2 (not_2_out, Y0);
  not not_3 (not_3_out, Y1);
  not not_4 (not_4_out, Y2);
  not not_5 (not_5_out, Y3);
  and and_2 (Z, not_2_out, not_3_out, not_4_out, not_5_out);
endmodule

module _2_1_Mux (
  input  Selector,
  input  A,
  input  B,
  output out_4
);

  wire and_1_out, and_2_out, not_1_out;

  not not_1 (not_1_out, Selector);
  and and_1 (and_1_out, Selector, A);
  and and_2 (and_2_out, not_1_out, B);
  or or_1 (out_4, and_1_out, and_2_out);
endmodule

module _4_1_mux (
  input  S1,
  input  D,
  input  S0,
  input  C,
  input  B,
  input  A,
  output out_7
);

  wire n2_1_mux_1_out_4, n2_1_mux_2_out_4;

  _2_1_Mux u_2_1_mux_1 (.Selector(S1), .A(D), .B(C), .out_4(n2_1_mux_1_out_4));
  _2_1_Mux u_2_1_mux_2 (.Selector(S1), .A(B), .B(A), .out_4(n2_1_mux_2_out_4));
  _2_1_Mux u_2_1_mux_3 (.Selector(S0), .A(n2_1_mux_1_out_4), .B(n2_1_mux_2_out_4), .out_4(out_7));
endmodule

module half_adder (
  input  A,
  input  B,
  output Sum,
  output Cout
);

  xor xor_1 (Sum, A, B);
  and and_1 (Cout, A, B);
endmodule

module Full_Adder_1bit (
  input  in_1,
  input  in_2,
  input  in_3,
  output sum,
  output Cout
);

  wire and_1_out, half_adder_1_cout, half_adder_1_sum;

  half_adder half_adder_1 (.A(in_2), .B(in_3), .Sum(half_adder_1_sum), .Cout(half_adder_1_cout));
  and and_1 (and_1_out, half_adder_1_sum, in_1);
  xor xor_1 (sum, in_1, half_adder_1_sum);
  or or_1 (Cout, half_adder_1_cout, and_1_out);
endmodule

module shifter (
  input  A0,
  input  A1,
  input  A2,
  input  A3,
  output S0,
  output S1,
  output S2,
  output S3
);

  _2_1_Mux u_2_1_mux_1 (.Selector(A0), .A(1'b1), .B(1'b0), .out_4(S1));
  _2_1_Mux u_2_1_mux_2 (.Selector(A1), .A(1'b1), .B(1'b0), .out_4(S2));
  _2_1_Mux u_2_1_mux_3 (.Selector(A2), .A(1'b1), .B(1'b0), .out_4(S3));

  assign S0 = A0;
endmodule

module Arithmetic_Unit_1bit (
  input  in_1,
  input  Cin,
  input  A,
  input  B,
  output sum,
  output cout
);

  wire n2_1_mux_1_out_4, not_1_out;

  not not_1 (not_1_out, B);
  _2_1_Mux u_2_1_mux_1 (.Selector(in_1), .A(B), .B(not_1_out), .out_4(n2_1_mux_1_out_4));
  Full_Adder_1bit full_adder_1bit_1 (.in_1(Cin), .in_2(n2_1_mux_1_out_4), .in_3(A), .sum(sum), .Cout(cout));
endmodule

module Logic_Unit_1bit (
  input  A,
  input  B,
  input  S0,
  input  S1,
  output out_5
);

  wire and_1_out, not_1_out, or_1_out, xor_1_out;

  and and_1 (and_1_out, A, B);
  or or_1 (or_1_out, A, B);
  xor xor_1 (xor_1_out, A, B);
  not not_1 (not_1_out, B);
  _4_1_mux u_4_1_mux_1 (.D(not_1_out), .C(xor_1_out), .B(or_1_out), .A(and_1_out), .out_7(out_5), .S1(S1), .S0(S0));
endmodule

module _4Bit_AU (
  input  S0,
  input  A3,
  input  B3,
  input  Cin,
  input  A2,
  input  B2,
  input  A1,
  input  B1,
  input  B0,
  input  A0,
  output Y0,
  output Y1,
  output Y2,
  output Y3,
  output V
);

  wire arithmetic_unit_1bit_1_cout, arithmetic_unit_1bit_2_cout, arithmetic_unit_1bit_3_cout;

  Arithmetic_Unit_1bit arithmetic_unit_1bit_1 (
    .A(A3), .B(B3), .sum(Y0), .Cin(Cin), .cout(arithmetic_unit_1bit_1_cout), .in_1(S0));
  Arithmetic_Unit_1bit arithmetic_unit_1bit_2 (
    .A(A2), .B(B2), .sum(Y1), .Cin(arithmetic_unit_1bit_1_cout), .cout(arithmetic_unit_1bit_2_cout), .in_1(S0));
  Arithmetic_Unit_1bit arithmetic_unit_1bit_3 (
    .A(A1), .B(B1), .sum(Y2), .Cin(arithmetic_unit_1bit_2_cout), .cout(arithmetic_unit_1bit_3_cout), .in_1(S0));
  Arithmetic_Unit_1bit arithmetic_unit_1bit_4 (
    .A(B0), .B(A0), .sum(Y3), .Cin(arithmetic_unit_1bit_3_cout), .cout(V), .in_1(S0));
endmodule

module _4Bit_LU (
  input  S0,
  input  S1,
  input  in_3,
  input  in_4,
  input  in_5,
  input  in_6,
  input  in_7,
  input  in_8,
  input  in_9,
  input  in_10,
  output out_11,
  output out_12,
  output out_13,
  output out_14
);

  Logic_Unit_1bit logic_unit_1bit_1 (.out_5(out_11), .A(in_3), .B(in_4), .S0(S0), .S1(S1));
  Logic_Unit_1bit logic_unit_1bit_2 (.out_5(out_12), .A(in_5), .B(in_6), .S0(S0), .S1(S1));
  Logic_Unit_1bit logic_unit_1bit_3 (.out_5(out_13), .A(in_7), .B(in_8), .S0(S0), .S1(S1));
  Logic_Unit_1bit logic_unit_1bit_4 (.out_5(out_14), .A(in_9), .B(in_10), .S0(S0), .S1(S1));
endmodule

module testing (
  input  S0,
  input  S1,
  input  S2,
  input  S3,
  input  A0,
  input  A1,
  input  A2,
  input  A3,
  input  B0,
  input  B1,
  input  B2,
  input  B3,
  output Y0,
  output Y1,
  output Y2,
  output out_16,
  output Y3,
  output out_18
);

  main main_1 (
    .A0(A0), .A1(A1), .A2(A2), .A3(A3), .B0(B0), .B1(B1), .B2(B2), .B3(B3), .Y0(Y0), .V(out_16), .Y1(Y1),
    .Y2(Y2), .Y3(Y3), .S1(S1), .S0(S0), .S2(S2), .S3(S3), .Z(out_18));
endmodule
